# Fritzing sketch TouchMe (saved by Fritzing 0.9.0b)
breadboards: 2

parts:
  LED1 = LED - 5mm [color="Red (633nm)" package="5 mm [THT]"]
  R1 = Resistor [tolerance=±5% resistance=220 package=THT]
  S1 = Pushbutton [package="[THT]"]
  J1 = Piezo Speaker
  Part1 = Arduino Uno (Rev3)
  LED2 = LED - 5mm [color="Yellow (592nm)" package="5 mm [THT]"]
  R3 = Resistor [tolerance=±5% resistance=220 package=THT]
  S2 = Pushbutton [package="[THT]"]

nets (from the breadboard view):
  N1: LED1.cathode, R1.Pin_1
  N2: LED1.anode, S1.Pin_3, S1.Pin_4, Part1.GND, LED2.anode, S2.Pin_3, S2.Pin_4
  N3: R1.Pin_0, Part1.D2
  N4: S1.Pin_1, S1.Pin_2, Part1.D6_PWM
  N5: J1.pin1, Part1.D10_PWM/SS
  N6: J1.pin2, Part1.5V
  N7: Part1.D3_PWM, R3.Pin_0
  N8: Part1.D7, S2.Pin_1, S2.Pin_2
  N9: LED2.cathode, R3.Pin_1
